// Logisim project MIPS.circ as structural Verilog: 4 circuits, main circuit main
module main (
  input  [3:0] RS,
  input  [3:0] RT,
  input  WC,
  input  [3:0] RD,
  input  [15:0] in_5,
  output [15:0] Read1,
  output [15:0] Read2
);

  wire clock_1_out;

  Clock clock_1 (.out(clock_1_out));
  REGFILE regfile_1 (.RS(RS), .RT(RT), .CLK(clock_1_out), .WC(WC), .WD(in_5), .RD(RD), .Read1(Read1), .Read2(Read2));
endmodule

module REGFILE (
  input  [3:0] RS,
  input  [3:0] RT,
  input  CLK,
  input  WC,
  input  [15:0] WD,
  input  [3:0] RD,
  output [15:0] Read1,
  output [15:0] Read2
);

  wire and_1_out, and_2_out, and_3_out, and_4_out, and_5_out, and_6_out, and_7_out, and_8_out, and_9_out,
       and_10_out, and_11_out, and_12_out, and_13_out, and_14_out, and_15_out, and_16_out, decoder_1_out0,
       decoder_1_out1, decoder_1_out2, decoder_1_out3, decoder_1_out4, decoder_1_out5, decoder_1_out6,
       decoder_1_out7, decoder_1_out8, decoder_1_out9, decoder_1_out10, decoder_1_out11, decoder_1_out12,
       decoder_1_out13, decoder_1_out14, decoder_1_out15;
  wire [15:0] register_1_q, register_2_q, register_3_q, register_4_q, register_5_q, register_6_q,
       register_7_q, register_8_q, register_9_q, register_10_q, register_11_q, register_12_q, register_13_q,
       register_14_q, register_15_q, register_16_q;

  Decoder #(.select(4)) decoder_1 (
    .out0(decoder_1_out0), .out1(decoder_1_out1), .out2(decoder_1_out2), .out3(decoder_1_out3),
    .out4(decoder_1_out4), .out5(decoder_1_out5), .out6(decoder_1_out6), .out7(decoder_1_out7),
    .out8(decoder_1_out8), .out9(decoder_1_out9), .out10(decoder_1_out10), .out11(decoder_1_out11),
    .out12(decoder_1_out12), .out13(decoder_1_out13), .out14(decoder_1_out14), .out15(decoder_1_out15),
    .sel(RD));  // open: en
  and and_1 (and_1_out, decoder_1_out0, WC);
  and and_2 (and_2_out, decoder_1_out1, WC);
  and and_3 (and_3_out, decoder_1_out2, WC);
  and and_4 (and_4_out, decoder_1_out3, WC);
  and and_5 (and_5_out, decoder_1_out4, WC);
  and and_6 (and_6_out, decoder_1_out5, WC);
  and and_7 (and_7_out, decoder_1_out6, WC);
  and and_8 (and_8_out, decoder_1_out7, WC);
  Register #(.width(16)) register_1 (.D(WD), .en(and_1_out), .clk(CLK), .Q(register_1_q));  // open: clr
  Register #(.width(16)) register_2 (.D(WD), .en(and_2_out), .clk(CLK), .Q(register_2_q));  // open: clr
  Register #(.width(16)) register_3 (.D(WD), .en(and_3_out), .clk(CLK), .Q(register_3_q));  // open: clr
  Register #(.width(16)) register_4 (.D(WD), .en(and_4_out), .clk(CLK), .Q(register_4_q));  // open: clr
  Register #(.width(16)) register_5 (.D(WD), .en(and_5_out), .clk(CLK), .Q(register_5_q));  // open: clr
  Register #(.width(16)) register_6 (.D(WD), .en(and_6_out), .clk(CLK), .Q(register_6_q));  // open: clr
  Register #(.width(16)) register_7 (.D(WD), .en(and_7_out), .clk(CLK), .Q(register_7_q));  // open: clr
  Register #(.width(16)) register_8 (.D(WD), .en(and_8_out), .clk(CLK), .Q(register_8_q));  // open: clr
  Register #(.width(16)) register_9 (.D(WD), .en(and_9_out), .clk(CLK), .Q(register_9_q));  // open: clr
  and and_9 (and_9_out, decoder_1_out8, WC);
  Register #(.width(16)) register_10 (.D(WD), .en(and_10_out), .clk(CLK), .Q(register_10_q));  // open: clr
  and and_10 (and_10_out, decoder_1_out9, WC);
  Register #(.width(16)) register_11 (.D(WD), .en(and_11_out), .clk(CLK), .Q(register_11_q));  // open: clr
  and and_11 (and_11_out, decoder_1_out10, WC);
  Register #(.width(16)) register_12 (.D(WD), .en(and_12_out), .clk(CLK), .Q(register_12_q));  // open: clr
  and and_12 (and_12_out, decoder_1_out11, WC);
  Register #(.width(16)) register_13 (.D(WD), .en(and_13_out), .clk(CLK), .Q(register_13_q));  // open: clr
  and and_13 (and_13_out, decoder_1_out12, WC);
  Register #(.width(16)) register_14 (.D(WD), .en(and_14_out), .clk(CLK), .Q(register_14_q));  // open: clr
  and and_14 (and_14_out, decoder_1_out13, WC);
  Register #(.width(16)) register_15 (.D(WD), .en(and_15_out), .clk(CLK), .Q(register_15_q));  // open: clr
  and and_15 (and_15_out, decoder_1_out14, WC);
  Register #(.width(16)) register_16 (.D(WD), .en(and_16_out), .clk(CLK), .Q(register_16_q));  // open: clr
  and and_16 (and_16_out, decoder_1_out15, WC);
  Multiplexer #(.select(4), .width(16)) multiplexer_1 (
    .in0(register_1_q), .in1(register_2_q), .in2(register_3_q), .in3(register_4_q), .in4(register_5_q),
    .in5(register_6_q), .in6(register_7_q), .in7(register_8_q), .in8(register_9_q), .in9(register_10_q),
    .in10(register_11_q), .in11(register_12_q), .in12(register_13_q), .in13(register_14_q),
    .in14(register_15_q), .in15(register_16_q), .out(Read1), .sel(RS));
  Multiplexer #(.select(4), .width(16)) multiplexer_2 (
    .in0(register_1_q), .in1(register_2_q), .in2(register_3_q), .in3(register_4_q), .in4(register_5_q),
    .in5(register_6_q), .in6(register_7_q), .in7(register_8_q), .in8(register_9_q), .in9(register_10_q),
    .in10(register_11_q), .in11(register_12_q), .in12(register_13_q), .in13(register_14_q),
    .in14(register_15_q), .in15(register_16_q), .out(Read2), .sel(RT));

  // Notes on the sheet:
  //   Priyo Raihan
  //   2311692042
endmodule

module OneBitALU (
  input  A,
  input  B,
  input  Cin,
  input  [1:0] Sel,
  input  Binv,
  output Y,
  output Cout
);

  wire adder_1_out, and_1_out, and_2_out, or_1_out, xor_1_out;

  and and_1 (and_1_out, Binv, Sel[0]);
  xor xor_1 (xor_1_out, B, and_1_out);
  Adder #(.width(1)) adder_1 (.a(A), .b(xor_1_out), .out(adder_1_out), .cin(Cin), .cout(Cout));
  and and_2 (and_2_out, A, B);
  or or_1 (or_1_out, A, B);
  Multiplexer #(.select(2)) multiplexer_1 (
    .in0(and_2_out), .in1(or_1_out), .in2(adder_1_out), .in3(adder_1_out), .out(Y), .sel(Sel));
endmodule

module ALU (
  input  [31:0] B,
  input  [31:0] A,
  input  Cin,
  input  Binv,
  input  [1:0] Sel,
  output [31:0] out_6,
  output Zero,
  output Cout
);

  wire onebitalu_1_cout, onebitalu_2_cout, onebitalu_3_cout, onebitalu_4_cout, onebitalu_5_cout,
       onebitalu_6_cout, onebitalu_7_cout, onebitalu_8_cout, onebitalu_9_cout, onebitalu_10_cout,
       onebitalu_11_cout, onebitalu_12_cout, onebitalu_13_cout, onebitalu_14_cout, onebitalu_15_cout,
       onebitalu_16_cout, onebitalu_17_cout, onebitalu_18_cout, onebitalu_19_cout, onebitalu_20_cout,
       onebitalu_21_cout, onebitalu_22_cout, onebitalu_23_cout, onebitalu_24_cout, onebitalu_25_cout,
       onebitalu_26_cout, onebitalu_27_cout, onebitalu_28_cout, onebitalu_29_cout, onebitalu_30_cout,
       onebitalu_31_cout;

  OneBitALU onebitalu_1 (.A(A[0]), .B(B[0]), .Cin(Cin), .Sel(Sel), .Binv(Binv), .Y(out_6[0]), .Cout(onebitalu_1_cout));
  OneBitALU onebitalu_2 (
    .A(A[1]), .B(B[1]), .Cin(onebitalu_1_cout), .Sel(Sel), .Binv(Binv), .Y(out_6[1]), .Cout(onebitalu_2_cout));
  OneBitALU onebitalu_3 (
    .A(A[2]), .B(B[2]), .Cin(onebitalu_2_cout), .Sel(Sel), .Binv(Binv), .Y(out_6[2]), .Cout(onebitalu_3_cout));
  OneBitALU onebitalu_4 (
    .A(A[3]), .B(B[3]), .Cin(onebitalu_3_cout), .Sel(Sel), .Binv(Binv), .Y(out_6[3]), .Cout(onebitalu_4_cout));
  OneBitALU onebitalu_5 (
    .A(A[4]), .B(B[4]), .Cin(onebitalu_4_cout), .Sel(Sel), .Binv(Binv), .Y(out_6[4]), .Cout(onebitalu_5_cout));
  OneBitALU onebitalu_6 (
    .A(A[5]), .B(B[5]), .Cin(onebitalu_5_cout), .Sel(Sel), .Binv(Binv), .Y(out_6[5]), .Cout(onebitalu_6_cout));
  OneBitALU onebitalu_7 (
    .A(A[6]), .B(B[6]), .Cin(onebitalu_6_cout), .Sel(Sel), .Binv(Binv), .Y(out_6[6]), .Cout(onebitalu_7_cout));
  OneBitALU onebitalu_8 (
    .A(A[7]), .B(B[7]), .Cin(onebitalu_7_cout), .Sel(Sel), .Binv(Binv), .Y(out_6[7]), .Cout(onebitalu_8_cout));
  OneBitALU onebitalu_9 (
    .A(A[8]), .B(B[8]), .Cin(onebitalu_8_cout), .Sel(Sel), .Binv(Binv), .Y(out_6[8]), .Cout(onebitalu_9_cout));
  OneBitALU onebitalu_10 (
    .A(A[9]), .B(B[9]), .Cin(onebitalu_9_cout), .Sel(Sel), .Binv(Binv), .Y(out_6[9]), .Cout(onebitalu_10_cout));
  OneBitALU onebitalu_11 (
    .A(A[10]), .B(B[10]), .Cin(onebitalu_10_cout), .Sel(Sel), .Binv(Binv), .Y(out_6[10]),
    .Cout(onebitalu_11_cout));
  OneBitALU onebitalu_12 (
    .A(A[11]), .B(B[11]), .Cin(onebitalu_11_cout), .Sel(Sel), .Binv(Binv), .Y(out_6[11]),
    .Cout(onebitalu_12_cout));
  OneBitALU onebitalu_13 (
    .A(A[12]), .B(B[12]), .Cin(onebitalu_12_cout), .Sel(Sel), .Binv(Binv), .Y(out_6[12]),
    .Cout(onebitalu_13_cout));
  OneBitALU onebitalu_14 (
    .A(A[13]), .B(B[13]), .Cin(onebitalu_13_cout), .Sel(Sel), .Binv(Binv), .Y(out_6[13]),
    .Cout(onebitalu_14_cout));
  OneBitALU onebitalu_15 (
    .A(A[14]), .B(B[14]), .Cin(onebitalu_14_cout), .Sel(Sel), .Binv(Binv), .Y(out_6[14]),
    .Cout(onebitalu_15_cout));
  OneBitALU onebitalu_16 (
    .A(A[15]), .B(B[15]), .Cin(onebitalu_15_cout), .Sel(Sel), .Binv(Binv), .Y(out_6[15]),
    .Cout(onebitalu_16_cout));
  OneBitALU onebitalu_17 (
    .A(A[16]), .B(B[16]), .Cin(onebitalu_16_cout), .Sel(Sel), .Binv(Binv), .Y(out_6[16]),
    .Cout(onebitalu_17_cout));
  OneBitALU onebitalu_18 (
    .A(A[17]), .B(B[17]), .Cin(onebitalu_17_cout), .Sel(Sel), .Binv(Binv), .Y(out_6[17]),
    .Cout(onebitalu_18_cout));
  OneBitALU onebitalu_19 (
    .A(A[18]), .B(B[18]), .Cin(onebitalu_18_cout), .Sel(Sel), .Binv(Binv), .Y(out_6[18]),
    .Cout(onebitalu_19_cout));
  OneBitALU onebitalu_20 (
    .A(A[19]), .B(B[19]), .Cin(onebitalu_19_cout), .Sel(Sel), .Binv(Binv), .Y(out_6[19]),
    .Cout(onebitalu_20_cout));
  OneBitALU onebitalu_21 (
    .A(A[20]), .B(B[20]), .Cin(onebitalu_20_cout), .Sel(Sel), .Binv(Binv), .Y(out_6[20]),
    .Cout(onebitalu_21_cout));
  OneBitALU onebitalu_22 (
    .A(A[21]), .B(B[21]), .Cin(onebitalu_21_cout), .Sel(Sel), .Binv(Binv), .Y(out_6[21]),
    .Cout(onebitalu_22_cout));
  OneBitALU onebitalu_23 (
    .A(A[22]), .B(B[22]), .Cin(onebitalu_22_cout), .Sel(Sel), .Binv(Binv), .Y(out_6[22]),
    .Cout(onebitalu_23_cout));
  OneBitALU onebitalu_24 (
    .A(A[23]), .B(B[23]), .Cin(onebitalu_23_cout), .Sel(Sel), .Binv(Binv), .Y(out_6[23]),
    .Cout(onebitalu_24_cout));
  OneBitALU onebitalu_25 (
    .A(A[24]), .B(B[24]), .Cin(onebitalu_24_cout), .Sel(Sel), .Binv(Binv), .Y(out_6[24]),
    .Cout(onebitalu_25_cout));
  OneBitALU onebitalu_26 (
    .A(A[25]), .B(B[25]), .Cin(onebitalu_25_cout), .Sel(Sel), .Binv(Binv), .Y(out_6[25]),
    .Cout(onebitalu_26_cout));
  OneBitALU onebitalu_27 (
    .A(A[26]), .B(B[26]), .Cin(onebitalu_26_cout), .Sel(Sel), .Binv(Binv), .Y(out_6[26]),
    .Cout(onebitalu_27_cout));
  OneBitALU onebitalu_28 (
    .A(A[27]), .B(B[27]), .Cin(onebitalu_27_cout), .Sel(Sel), .Binv(Binv), .Y(out_6[27]),
    .Cout(onebitalu_28_cout));
  OneBitALU onebitalu_29 (
    .A(A[28]), .B(B[28]), .Cin(onebitalu_28_cout), .Sel(Sel), .Binv(Binv), .Y(out_6[28]),
    .Cout(onebitalu_29_cout));
  OneBitALU onebitalu_30 (
    .A(A[29]), .B(B[29]), .Cin(onebitalu_29_cout), .Sel(Sel), .Binv(Binv), .Y(out_6[29]),
    .Cout(onebitalu_30_cout));
  OneBitALU onebitalu_31 (
    .A(A[30]), .B(B[30]), .Cin(onebitalu_30_cout), .Sel(Sel), .Binv(Binv), .Y(out_6[30]),
    .Cout(onebitalu_31_cout));
  OneBitALU onebitalu_32 (
    .A(A[31]), .B(B[31]), .Cin(onebitalu_31_cout), .Sel(Sel), .Binv(Binv), .Y(out_6[31]), .Cout(Cout));
  nor nor_1 (Zero, out_6[0], out_6[1], out_6[2], out_6[3], out_6[4], out_6[5], out_6[6], out_6[7], out_6[8], out_6[9], out_6[10], out_6[11], out_6[12], out_6[13], out_6[14], out_6[15], out_6[16], out_6[17], out_6[18], out_6[19], out_6[20], out_6[21], out_6[22], out_6[23], out_6[24], out_6[25], out_6[26], out_6[27], out_6[28], out_6[29], out_6[30], out_6[31]);
endmodule
